// Logisim project g2.circ as structural Verilog: 20 circuits, main circuit CPU
module _1_bit_sum (
  input  cin,
  input  a,
  input  b,
  output out_4
);

  wire and_1_out, and_2_out, and_3_out, and_4_out;

  and and_1 (and_1_out, ~cin, a, ~b);  // AND_Gate
  and and_2 (and_2_out, ~cin, ~a, b);  // AND_Gate
  and and_3 (and_3_out, cin, ~a, ~b);  // AND_Gate
  and and_4 (and_4_out, cin, a, b);
  or or_1 (out_4, and_1_out, and_2_out, and_3_out, and_4_out);
endmodule

module _1_bit_carryout (
  input  cin,
  input  a,
  input  b,
  output out_4
);

  wire and_1_out, and_2_out, and_3_out;

  and and_1 (and_1_out, cin, a);
  and and_2 (and_2_out, cin, b);
  and and_3 (and_3_out, a, b);
  or or_1 (out_4, and_1_out, and_2_out, and_3_out);
endmodule

module _1_bit_full_adder (
  input  cin,
  input  a,
  input  b,
  output sum,
  output cout
);

  _1_bit_sum u_1_bit_sum_1 (.cin(cin), .a(a), .b(b), .out_4(sum));
  _1_bit_carryout u_1_bit_carryout_1 (.cin(cin), .a(a), .b(b), .out_4(cout));
endmodule

module _1_bit_ALU (
  input  ainvert,
  input  binvert,
  input  cin,
  input  [1:0] op,
  input  a,
  input  b,
  input  less,
  output result,
  output cout
);

  wire and_1_out, multiplexer_1_out, multiplexer_2_out, n1_bit_full_adder_1_sum, not_1_out, not_2_out,
       or_1_out;

  Multiplexer multiplexer_1 (.in0(a), .in1(not_1_out), .out(multiplexer_1_out), .sel(ainvert));
  not not_1 (not_1_out, a);
  not not_2 (not_2_out, b);
  Multiplexer multiplexer_2 (.in0(b), .in1(not_2_out), .out(multiplexer_2_out), .sel(binvert));
  and and_1 (and_1_out, multiplexer_1_out, multiplexer_2_out);
  or or_1 (or_1_out, multiplexer_1_out, multiplexer_2_out);
  _1_bit_full_adder u_1_bit_full_adder_1 (
    .a(multiplexer_1_out), .b(multiplexer_2_out), .cin(cin), .cout(cout), .sum(n1_bit_full_adder_1_sum));
  Multiplexer #(.select(2)) multiplexer_3 (
    .in0(and_1_out), .in1(or_1_out), .in2(n1_bit_full_adder_1_sum), .in3(less), .out(result), .sel(op));
endmodule

module Overflow_detection (
  input  cin,
  input  cout,
  output Overflow
);

  wire and_1_out, and_2_out;

  and and_1 (and_1_out, ~cin, cout);  // AND_Gate
  and and_2 (and_2_out, cin, ~cout);  // AND_Gate
  or or_1 (Overflow, and_1_out, and_2_out);
endmodule

module _1_bit_ALU_overflow_detect (
  input  ainvert,
  input  binvert,
  input  cin,
  input  [1:0] op,
  input  a,
  input  b,
  input  less,
  output result,
  output set,
  output Overflow
);

  wire and_1_out, multiplexer_1_out, multiplexer_2_out, n1_bit_full_adder_1_cout, not_1_out, not_2_out,
       or_1_out;

  Multiplexer multiplexer_1 (.in0(a), .in1(not_1_out), .out(multiplexer_1_out), .sel(ainvert));
  not not_1 (not_1_out, a);
  not not_2 (not_2_out, b);
  Multiplexer multiplexer_2 (.in0(b), .in1(not_2_out), .out(multiplexer_2_out), .sel(binvert));
  and and_1 (and_1_out, multiplexer_1_out, multiplexer_2_out);
  or or_1 (or_1_out, multiplexer_1_out, multiplexer_2_out);
  _1_bit_full_adder u_1_bit_full_adder_1 (
    .a(multiplexer_1_out), .b(multiplexer_2_out), .cin(cin), .cout(n1_bit_full_adder_1_cout), .sum(set));
  Overflow_detection overflow_detection_1 (.cin(cin), .cout(n1_bit_full_adder_1_cout), .Overflow(Overflow));
  Multiplexer #(.select(2)) multiplexer_3 (
    .in0(and_1_out), .in1(or_1_out), .in2(set), .in3(less), .out(result), .sel(op));
endmodule

module _4_bit_ALU (
  input  [3:0] Control,
  input  [3:0] a,
  input  [3:0] b,
  output [3:0] result,
  output Zero,
  output Overflow
);

  wire n1_bit_alu_1_cout, n1_bit_alu_2_cout, n1_bit_alu_3_cout, n1_bit_alu_overflow_detect_1_set, or_1_out;

  _1_bit_ALU u_1_bit_alu_1 (
    .a(a[0]), .b(b[0]), .less(n1_bit_alu_overflow_detect_1_set), .ainvert(Control[3]), .binvert(Control[2]),
    .cin(Control[2]), .op(Control[1:0]), .cout(n1_bit_alu_1_cout), .result(result[0]));
  _1_bit_ALU u_1_bit_alu_2 (
    .a(a[1]), .b(b[1]), .less(1'b0), .ainvert(Control[3]), .binvert(Control[2]), .cin(n1_bit_alu_1_cout),
    .op(Control[1:0]), .cout(n1_bit_alu_2_cout), .result(result[1]));
  _1_bit_ALU u_1_bit_alu_3 (
    .a(a[2]), .b(b[2]), .less(1'b0), .ainvert(Control[3]), .binvert(Control[2]), .cin(n1_bit_alu_2_cout),
    .op(Control[1:0]), .cout(n1_bit_alu_3_cout), .result(result[2]));
  _1_bit_ALU_overflow_detect u_1_bit_alu_overflow_detect_1 (
    .a(a[3]), .b(b[3]), .less(1'b0), .ainvert(Control[3]), .binvert(Control[2]), .cin(n1_bit_alu_3_cout),
    .op(Control[1:0]), .result(result[3]), .set(n1_bit_alu_overflow_detect_1_set), .Overflow(Overflow));
  or or_1 (or_1_out, result[0], result[1], result[2], result[3]);
  not not_1 (Zero, or_1_out);
endmodule

module _16_32_bit_extender (
  input  SignExtend,
  input  [15:0] in,
  output [31:0] out
);

  Multiplexer #(.width(32)) multiplexer_1 (
    .in0({{16{1'b0}}, in}), .in1({{17{in[15]}}, in[14:0]}), .out(out), .sel(SignExtend));
endmodule

module Control (
  input  [5:0] Instruction_input,
  output SignExtend,
  output Jump,
  output Link,
  output [11:0] Control_to_MUX
);

  PLA #(.in_width(6), .out_width(11), .truth_table("000000,00010010001#R-instructions\n001001,00101010000#addiu\n00110x,00001010000#andi/ori\n000100,00100000010#beq\n101011,00001000100#sw\n100011,00001111000#lw\n001010,00101010000#slti\n000010,01000000000#j\n000011,11010010001#jal")) pla_1 ();  // open: in, out
  // PLA #(.in_width(6), .out_width(4), .truth_table("001001,0010#addiu\n001100,0000#andi\n001101,0001#ori\n001010,0111#slti\n10x011,0010#sw og lw\n000100,0110#beq\n000011,0010#")) pla_2: pin names not known; wires that end beside it: Control_to_MUX[11:8]
endmodule

module ALU_Control (
  input  [3:0] immidiate_input,
  input  [5:0] funct,
  input  ALUOp_in,
  output jr,
  output [3:0] ALU_input
);

  wire [3:0] pla_1_out;

  PLA #(.in_width(6), .out_width(5), .truth_table("100001,00010#addu\n100011,00110#subu\n100100,00000#and\n100101,00001#or\n101010,00111#slt\n001000,10110#jr")) pla_1 (.out(pla_1_out));  // open: in
  Multiplexer #(.width(4)) multiplexer_1 (.in0(immidiate_input), .in1(pla_1_out), .out(ALU_input), .sel(ALUOp_in));
endmodule

module IF_ID (
  input  stall,
  input  [31:0] PC_input,
  input  [31:0] Instruction_input,
  input  Clock,
  output [31:0] PC_output,
  output [31:0] Instruction_output
);

  wire not_1_out;

  not not_1 (not_1_out, stall);
  Register #(.width(32)) register_1 (.D(PC_input), .en(not_1_out), .Q(PC_output), .clk(Clock));  // open: clr
  Register #(.width(32)) register_2 (
    .D(Instruction_input), .en(not_1_out), .Q(Instruction_output), .clk(Clock));  // open: clr
endmodule

module CPU (
);

  wire alu_control_1_jr, and_1_out, and_2_out, clock_1_out, comparator_1_eq, control_1_jump, control_1_link,
       control_1_signextend, hazard_detection_1_stall, mips_alu_1_p4, not_1_out, or_1_out, or_2_out;
  wire [1:0] ex_mem_1_m_output, ex_mem_1_wb_output, forwarding_unit_1_forward_a, forwarding_unit_1_forward_b,
       id_ex_1_m_output, id_ex_1_wb_output, registerfile_1_p3;
  wire [3:0] alu_control_1_alu_input;
  wire [4:0] ex_mem_1_regdst_output, id_ex_1_rd_output, id_ex_1_rs_output, id_ex_1_rt_output,
       multiplexer_4_out, multiplexer_5_out, multiplexer_9_out, multiplexer_10_out, registerfile_1_p4;
  wire [5:0] id_ex_1_signextend_output;
  wire [7:0] id_ex_1_ex_output;
  wire [11:0] control_1_control_to_mux, multiplexer_6_out;
  wire [27:0] if_id_1_pc_output;
  wire [31:0] adder_1_out, adder_2_out, ex_mem_1_alu_res_output, ex_mem_1_read_data2_output,
       id_ex_1_pc_output, id_ex_1_read_data1_output, id_ex_1_read_data2_output, mem_wb_1_address_output,
       mem_wb_1_read_data_output, mips_alu_1_p5, mips_ram_1_p6, mipsprogramrom_1_p2, multiplexer_1_out,
       multiplexer_2_out, multiplexer_3_out, multiplexer_7_out, multiplexer_8_out, multiplexer_11_out,
       multiplexer_12_out, multiplexer_13_out, multiplexer_14_out, n16_32_bit_extender_1_out, register_1_q,
       registerfile_1_p1, registerfile_1_p7, registerfile_1_p8, shifter_1_out;
  wire [31:2] if_id_1_instruction_output;
  wire [31:6] id_ex_1_signextend_output_2;
  wire [31:26] if_id_1_instruction_output_2;

  Multiplexer #(.width(32)) multiplexer_1 (
    .in0(multiplexer_2_out), .in1(multiplexer_14_out), .out(multiplexer_1_out), .sel(and_2_out));
  Multiplexer #(.width(32)) multiplexer_2 (
    .in0(adder_1_out), .in1({if_id_1_instruction_output, 2'b00}), .out(multiplexer_2_out),
    .sel(control_1_jump));
  Register #(.width(32)) register_1 (
    .D(multiplexer_1_out), .en(not_1_out), .Q(register_1_q), .clk(clock_1_out));  // open: clr
  not not_1 (not_1_out, hazard_detection_1_stall);
  Clock clock_1 (.out(clock_1_out));
  Adder #(.width(32)) adder_1 (.a(register_1_q), .b(32'h4), .out(adder_1_out));  // open: cin, cout
  or or_1 (or_1_out, and_2_out, control_1_jump);
  // MIPSProgramROM mipsprogramrom_1: pin names not known; wires that end beside it: register_1_q, mipsprogramrom_1_p2
  Hazard_detection hazard_detection_1 (
    .ID_EX_MemRead(id_ex_1_m_output[1]), .ID_EX_RegisterRt(id_ex_1_rt_output),
    .IF_ID_RegisterRs(if_id_1_instruction_output[27:23]),
    .IF_ID_RegisterRt(if_id_1_instruction_output[22:18]), .stall(hazard_detection_1_stall));
  IF_ID if_id_1 (
    .PC_input(adder_1_out), .Instruction_input(multiplexer_3_out), .stall(hazard_detection_1_stall),
    .Clock(clock_1_out), .PC_output({if_id_1_instruction_output[31:28], if_id_1_pc_output}),
    .Instruction_output({if_id_1_instruction_output_2, if_id_1_instruction_output[27:2]}));
  Multiplexer #(.width(32)) multiplexer_3 (
    .in0(mipsprogramrom_1_p2), .in1({32{1'b0}}), .out(multiplexer_3_out), .sel(or_1_out));
  Comparator #(.width(6)) comparator_1 (
    .a(if_id_1_instruction_output[7:2]), .b(6'b001000), .eq(comparator_1_eq));  // open: gt, lt
  Control control_1 (
    .Instruction_input(if_id_1_instruction_output_2), .SignExtend(control_1_signextend),
    .Jump(control_1_jump), .Link(control_1_link), .Control_to_MUX(control_1_control_to_mux));
  and and_1 (and_1_out, ~and_2_out, ~hazard_detection_1_stall);  // AND_Gate
  _16_32_bit_extender u_16_32_bit_extender_1 (
    .in(if_id_1_instruction_output[17:2]), .SignExtend(control_1_signextend), .out(n16_32_bit_extender_1_out));
  Multiplexer #(.width(5)) multiplexer_4 (
    .in0(if_id_1_instruction_output[22:18]), .in1({5{1'b1}}), .out(multiplexer_4_out), .sel(comparator_1_eq));
  Multiplexer #(.width(5)) multiplexer_5 (
    .in0(if_id_1_instruction_output[27:23]), .in1({5{1'b1}}), .out(multiplexer_5_out), .sel(comparator_1_eq));
  Multiplexer #(.width(12)) multiplexer_6 (
    .in0({12{1'b0}}), .in1(control_1_control_to_mux), .out(multiplexer_6_out), .sel(and_1_out));
  // RegisterFile #(.trigger("falling")) registerfile_1: pin names not known; wires that end beside it: registerfile_1_p1, clock_1_out, registerfile_1_p3[0], registerfile_1_p4, multiplexer_5_out, multiplexer_4_out, registerfile_1_p7, registerfile_1_p8
  Multiplexer #(.width(32)) multiplexer_7 (
    .in0(registerfile_1_p7), .in1({if_id_1_instruction_output[31:28], if_id_1_pc_output}),
    .out(multiplexer_7_out), .sel(control_1_link));
  Multiplexer #(.width(32)) multiplexer_8 (
    .in0(registerfile_1_p8), .in1({if_id_1_instruction_output[31:28], if_id_1_pc_output}),
    .out(multiplexer_8_out), .sel(control_1_link));
  Multiplexer #(.width(5)) multiplexer_9 (
    .in0(if_id_1_instruction_output[17:13]), .in1({5{1'b1}}), .out(multiplexer_9_out), .sel(control_1_link));
  ID_EX id_ex_1 (
    .WB_input(multiplexer_6_out[5:4]), .M_input(multiplexer_6_out[3:2]),
    .EX_input({multiplexer_6_out[11:6], multiplexer_6_out[1:0]}),
    .PC_input({if_id_1_instruction_output[31:28], if_id_1_pc_output}), .Read_Data1_input(multiplexer_7_out),
    .Read_Data2_input(multiplexer_8_out), .Signextend_input(n16_32_bit_extender_1_out),
    .rs_input(multiplexer_5_out), .rt_input(multiplexer_4_out), .rd_input(multiplexer_9_out),
    .Clock(clock_1_out), .WB_output(id_ex_1_wb_output), .M_output(id_ex_1_m_output),
    .EX_output(id_ex_1_ex_output), .PC_output(id_ex_1_pc_output),
    .Read_Data1_output(id_ex_1_read_data1_output), .Read_Data2_output(id_ex_1_read_data2_output),
    .Signextend_output({id_ex_1_signextend_output_2, id_ex_1_signextend_output}),
    .rs_output(id_ex_1_rs_output), .rt_output(id_ex_1_rt_output), .rd_output(id_ex_1_rd_output));
  ALU_Control alu_control_1 (
    .funct(id_ex_1_signextend_output), .ALUOp_in(id_ex_1_ex_output[0]),
    .immidiate_input(id_ex_1_ex_output[7:4]), .jr(alu_control_1_jr), .ALU_input(alu_control_1_alu_input));
  Multiplexer #(.width(5)) multiplexer_10 (
    .in0(id_ex_1_rt_output), .in1(id_ex_1_rd_output), .out(multiplexer_10_out), .sel(id_ex_1_ex_output[3]));
  Shifter #(.width(32)) shifter_1 (
    .in({id_ex_1_signextend_output_2, id_ex_1_signextend_output}), .\dist (5'b00010), .out(shifter_1_out));
  Multiplexer #(.select(2), .width(32)) multiplexer_11 (
    .in0(id_ex_1_read_data1_output), .in1(registerfile_1_p1), .in2(ex_mem_1_alu_res_output),
    .out(multiplexer_11_out), .sel(forwarding_unit_1_forward_a));  // open: in3
  Multiplexer #(.select(2), .width(32)) multiplexer_12 (
    .in0(id_ex_1_read_data2_output), .in1(registerfile_1_p1), .in2(ex_mem_1_alu_res_output),
    .out(multiplexer_12_out), .sel(forwarding_unit_1_forward_b));  // open: in3
  Forwarding_unit forwarding_unit_1 (
    .ID_EX_rs_input(id_ex_1_rs_output), .ID_EX_rt_input(id_ex_1_rt_output),
    .Forward_B(forwarding_unit_1_forward_b), .Forward_A(forwarding_unit_1_forward_a),
    .EX_MEM_regdst_input(ex_mem_1_regdst_output), .EX_MEM_wb_input(ex_mem_1_wb_output),
    .MEM_WB_regdts_input(registerfile_1_p4), .MEM_WB_wb_input(registerfile_1_p3));
  Adder #(.width(32)) adder_2 (.a(id_ex_1_pc_output), .b(shifter_1_out), .out(adder_2_out));  // open: cin, cout
  Multiplexer #(.width(32)) multiplexer_13 (
    .in0(multiplexer_12_out), .in1({id_ex_1_signextend_output_2, id_ex_1_signextend_output}),
    .out(multiplexer_13_out), .sel(id_ex_1_ex_output[2]));
  // Mips_ALU mips_alu_1: pin names not known; wires that end beside it: multiplexer_11_out, multiplexer_13_out, alu_control_1_alu_input, mips_alu_1_p4, mips_alu_1_p5
  or or_2 (or_2_out, alu_control_1_jr, id_ex_1_ex_output[1]);
  Multiplexer #(.width(32)) multiplexer_14 (
    .in0(adder_2_out), .in1(multiplexer_11_out), .out(multiplexer_14_out), .sel(alu_control_1_jr));
  and and_2 (and_2_out, or_2_out, mips_alu_1_p4);
  EX_MEM ex_mem_1 (
    .WB_input(id_ex_1_wb_output), .M_input(id_ex_1_m_output), .ALU_res_input(mips_alu_1_p5),
    .Read_Data2_input(id_ex_1_read_data2_output), .RegDst_input(multiplexer_10_out), .Clock(clock_1_out),
    .WB_output(ex_mem_1_wb_output), .M_output(ex_mem_1_m_output), .ALU_res_output(ex_mem_1_alu_res_output),
    .Read_Data2_output(ex_mem_1_read_data2_output), .RegDst_output(ex_mem_1_regdst_output));
  // MIPS_RAM #(.addrWidth(24)) mips_ram_1: pin names not known; wires that end beside it: ex_mem_1_alu_res_output[23:0], ex_mem_1_read_data2_output, ex_mem_1_m_output[0], ex_mem_1_m_output[1], clock_1_out, mips_ram_1_p6
  MEM_WB mem_wb_1 (
    .WB_input(ex_mem_1_wb_output), .Read_Data_input(mips_ram_1_p6), .Address_input(ex_mem_1_alu_res_output),
    .RegDst_input(ex_mem_1_regdst_output), .Clock(clock_1_out), .WB_output(registerfile_1_p3),
    .Read_Data_output(mem_wb_1_read_data_output), .Address_output(mem_wb_1_address_output),
    .RegDst_output(registerfile_1_p4));
  Multiplexer #(.width(32)) multiplexer_15 (
    .in0(mem_wb_1_address_output), .in1(mem_wb_1_read_data_output), .out(registerfile_1_p1),
    .sel(registerfile_1_p3[1]));

  // Notes on the sheet:
  //   contents of mipsprogramrom_1 (hex, n*v repeats v):
  //   addiu $1, $0, 0x1               # $1 = 0 + 1 = 0x1 addiu $2, $0, 0xc               # $2 = 0 + 12 =
  //   0xc addiu $3, $0, 0xffff            # $3 = 0 + 0xffff = 0xffffffff (pga sign extend) addu  $4, $1,
  //   $2                # $4 = 1 + 12 = 0xd subu  $5, $2, $1                # $5 = 12 - 1 = 0xb subu  $6,
  //   $1, $2                # $6 = 00000001 - 12 = 0xfffffff5 and   $7, $4, $5                # $7 = 1011
  //   and 1101 = 0x9 and   $8, $0, $5                # $8 = 0000 and 1011 = 0x0 or    $9, $4, $5
  //   # $9 = 1101 or 1011 = 0xf or    $10, $5, $0               # $10 = 1011 or 0000 =0xb slt   $11, $2,
  //   $5               # $11 = 12 < 11 = 0 slt   $12, $5, $2               # $12 = 11 < 12 = 1 andi  $13,
  //   $2, 0x6              # $13 = 1100 and 0110 = 0x4 andi  $14, $0, 0xffff           # $14 = 0 and
  //   0xffff = 0x0 sw    $7, 4($1)                 # store the contents of $7 (0x9) in memory 0x4 lw
  //   $15, 4($1)                # read memory 0x4 into register 15 (9) slti  $16, $2, 0xa              #
  //   $16 = 12 < 10 = 0 slti  $17, $2, 0xff             # $17 = 12 < 0xff = 1 ori   $20, $10, 0x2
  //   # $20 = 0xb or 0x2 = 0xf ori   $21, $13, 0x8             # $21 = 0x4 or 0x8 = 0xc  addu $18, $1, $0
  //   # load contents of $1 into $18, $18 = 1 Loop:   addiu $18, $18, 0x1     # add one to $18
  //   slti $19, $18, 0x5      # check if 18 is still less than 5         beq $19, $zero, Exit    # if it
  //   isn't we're done, go out of the loop         jal Loop  # if it is, loop again.  Exit:
  //   addu $21, $4, $5         addu $22, $4, $5         jr   $31
endmodule

module ID_EX (
  input  [1:0] WB_input,
  input  [1:0] M_input,
  input  [7:0] EX_input,
  input  [31:0] PC_input,
  input  [31:0] Read_Data1_input,
  input  [31:0] Read_Data2_input,
  input  [31:0] Signextend_input,
  input  [4:0] rs_input,
  input  [4:0] rt_input,
  input  [4:0] rd_input,
  input  Clock,
  output [1:0] WB_output,
  output [1:0] M_output,
  output [7:0] EX_output,
  output [31:0] PC_output,
  output [31:0] Read_Data1_output,
  output [31:0] Read_Data2_output,
  output [31:0] Signextend_output,
  output [4:0] rs_output,
  output [4:0] rt_output,
  output [4:0] rd_output
);

  Register #(.width(2)) register_1 (.D(WB_input), .Q(WB_output), .clk(Clock));  // open: en, clr
  Register #(.width(2)) register_2 (.D(M_input), .Q(M_output), .clk(Clock));  // open: en, clr
  Register register_3 (.D(EX_input), .Q(EX_output), .clk(Clock));  // open: en, clr
  Register #(.width(32)) register_4 (.D(PC_input), .Q(PC_output), .clk(Clock));  // open: en, clr
  Register #(.width(32)) register_5 (.D(Read_Data1_input), .Q(Read_Data1_output), .clk(Clock));  // open: en, clr
  Register #(.width(32)) register_6 (.D(Read_Data2_input), .Q(Read_Data2_output), .clk(Clock));  // open: en, clr
  Register #(.width(32)) register_7 (.D(Signextend_input), .Q(Signextend_output), .clk(Clock));  // open: en, clr
  Register #(.width(5)) register_8 (.D(rs_input), .Q(rs_output), .clk(Clock));  // open: en, clr
  Register #(.width(5)) register_9 (.D(rt_input), .Q(rt_output), .clk(Clock));  // open: en, clr
  Register #(.width(5)) register_10 (.D(rd_input), .Q(rd_output), .clk(Clock));  // open: en, clr
endmodule

module EX_MEM (
  input  [1:0] WB_input,
  input  [1:0] M_input,
  input  [31:0] ALU_res_input,
  input  [31:0] Read_Data2_input,
  input  [4:0] RegDst_input,
  input  Clock,
  output [1:0] WB_output,
  output [1:0] M_output,
  output [31:0] ALU_res_output,
  output [31:0] Read_Data2_output,
  output [4:0] RegDst_output
);

  Register #(.width(2)) register_1 (.D(WB_input), .Q(WB_output), .clk(Clock));  // open: en, clr
  Register #(.width(2)) register_2 (.D(M_input), .Q(M_output), .clk(Clock));  // open: en, clr
  Register #(.width(32)) register_3 (.D(ALU_res_input), .Q(ALU_res_output), .clk(Clock));  // open: en, clr
  Register #(.width(32)) register_4 (.D(Read_Data2_input), .Q(Read_Data2_output), .clk(Clock));  // open: en, clr
  Register #(.width(5)) register_5 (.D(RegDst_input), .Q(RegDst_output), .clk(Clock));  // open: en, clr
endmodule

module MEM_WB (
  input  [1:0] WB_input,
  input  [31:0] Read_Data_input,
  input  [31:0] Address_input,
  input  [4:0] RegDst_input,
  input  Clock,
  output [1:0] WB_output,
  output [31:0] Read_Data_output,
  output [31:0] Address_output,
  output [4:0] RegDst_output
);

  Register #(.width(2)) register_1 (.D(WB_input), .Q(WB_output), .clk(Clock));  // open: en, clr
  Register #(.width(32)) register_2 (.D(Read_Data_input), .Q(Read_Data_output), .clk(Clock));  // open: en, clr
  Register #(.width(32)) register_3 (.D(Address_input), .Q(Address_output), .clk(Clock));  // open: en, clr
  Register #(.width(5)) register_4 (.D(RegDst_input), .Q(RegDst_output), .clk(Clock));  // open: en, clr
endmodule

module Forwarding_unit (
  input  [4:0] EX_MEM_regdst_input,
  input  [1:0] EX_MEM_wb_input,
  input  [4:0] MEM_WB_regdts_input,
  input  [4:0] ID_EX_rs_input,
  input  [1:0] MEM_WB_wb_input,
  input  [4:0] ID_EX_rt_input,
  output [1:0] Forward_B,
  output [1:0] Forward_A
);

  EX_hazard ex_hazard_1 (
    .Forward_B(Forward_B[1]), .Forward_A(Forward_A[1]), .ID_EX_rt_input(ID_EX_rt_input),
    .EX_MEM_RegWrite(EX_MEM_wb_input[0]), .ID_EX_rs_input(ID_EX_rs_input),
    .EX_MEM_regdst_input(EX_MEM_regdst_input));
  MEM_hazard mem_hazard_1 (
    .Forward_B(Forward_B[0]), .Forward_A(Forward_A[0]), .EX_MEM_RegWrite(EX_MEM_wb_input[0]),
    .EX_MEM_regdst_input(EX_MEM_regdst_input), .ID_EX_rt_input(ID_EX_rt_input),
    .MEM_WB_RegWrite(MEM_WB_wb_input[0]), .ID_EX_rs_input(ID_EX_rs_input),
    .MEM_WB_regdst_input(MEM_WB_regdts_input));
endmodule

module equal (
  input  [4:0] in_1,
  input  [4:0] in_2,
  output out_3
);

  Comparator #(.width(5)) comparator_1 (.a(in_1), .b(in_2), .eq(out_3));  // open: gt, lt
endmodule

module EX_hazard (
  input  [4:0] ID_EX_rt_input,
  input  EX_MEM_RegWrite,
  input  [4:0] ID_EX_rs_input,
  input  [4:0] EX_MEM_regdst_input,
  output Forward_B,
  output Forward_A
);

  wire equal_1_out_3, equal_2_out_3, equal_3_out_3, not_1_out;

  and and_1 (Forward_B, EX_MEM_RegWrite, equal_1_out_3, not_1_out);
  equal equal_1 (.out_3(equal_1_out_3), .in_1(ID_EX_rt_input), .in_2(EX_MEM_regdst_input));
  and and_2 (Forward_A, EX_MEM_RegWrite, equal_2_out_3, not_1_out);
  equal equal_2 (.out_3(equal_2_out_3), .in_1(ID_EX_rs_input), .in_2(EX_MEM_regdst_input));
  not not_1 (not_1_out, equal_3_out_3);
  equal equal_3 (.out_3(equal_3_out_3), .in_1(EX_MEM_regdst_input), .in_2({5{1'b0}}));
endmodule

module MEM_hazard (
  input  EX_MEM_RegWrite,
  input  [4:0] EX_MEM_regdst_input,
  input  [4:0] ID_EX_rt_input,
  input  MEM_WB_RegWrite,
  input  [4:0] ID_EX_rs_input,
  input  [4:0] MEM_WB_regdst_input,
  output Forward_B,
  output Forward_A
);

  wire equal_1_out_3, equal_2_out_3, equal_3_out_3, ex_hazard_1_forward_a, ex_hazard_1_forward_b, not_1_out,
       not_2_out, not_3_out;

  not not_1 (not_1_out, ex_hazard_1_forward_b);
  not not_2 (not_2_out, ex_hazard_1_forward_a);
  EX_hazard ex_hazard_1 (
    .Forward_B(ex_hazard_1_forward_b), .Forward_A(ex_hazard_1_forward_a), .ID_EX_rt_input(ID_EX_rt_input),
    .EX_MEM_RegWrite(EX_MEM_RegWrite), .ID_EX_rs_input(ID_EX_rs_input),
    .EX_MEM_regdst_input(EX_MEM_regdst_input));
  and and_1 (Forward_B, not_1_out, equal_1_out_3, MEM_WB_RegWrite, not_3_out);
  equal equal_1 (.out_3(equal_1_out_3), .in_1(ID_EX_rt_input), .in_2(MEM_WB_regdst_input));
  and and_2 (Forward_A, not_2_out, equal_2_out_3, MEM_WB_RegWrite, not_3_out);
  equal equal_2 (.out_3(equal_2_out_3), .in_1(ID_EX_rs_input), .in_2(MEM_WB_regdst_input));
  not not_3 (not_3_out, equal_3_out_3);
  equal equal_3 (.out_3(equal_3_out_3), .in_1(MEM_WB_regdst_input), .in_2({5{1'b0}}));
endmodule

module Hazard_detection (
  input  ID_EX_MemRead,
  input  [4:0] ID_EX_RegisterRt,
  input  [4:0] IF_ID_RegisterRs,
  input  [4:0] IF_ID_RegisterRt,
  output stall
);

  wire equal_1_out_3, equal_2_out_3, or_1_out;

  equal equal_1 (.out_3(equal_1_out_3), .in_1(ID_EX_RegisterRt), .in_2(IF_ID_RegisterRs));
  equal equal_2 (.out_3(equal_2_out_3), .in_1(ID_EX_RegisterRt), .in_2(IF_ID_RegisterRt));
  or or_1 (or_1_out, equal_1_out_3, equal_2_out_3);
  and and_1 (stall, ID_EX_MemRead, or_1_out);
endmodule
